# Fritzing sketch stopwatch (saved by Fritzing 0.9.2b)
breadboards: 1

parts:
  Bauteil1 = Arduino Uno (Rev3)
  JY-MCU = JY-MCU
  R1 = Resistor [tolerance=±5% resistance=15k package=THT]
  R2 = Resistor [tolerance=±5% resistance=10k package=THT]
  Power_plug1 = Power plug
  TRS1 = Audio Jack (TRS) 3.5mm [package="4Ucon 08780 [THT]"]
  R3 = Resistor [tolerance=±5% resistance=15k package=THT]
  R4 = Resistor [tolerance=±5% resistance=10k package=THT]
  TRS2 = Audio Jack (TRS) 3.5mm [package="4Ucon 08780 [THT]"]
  R5 = Resistor [tolerance=±5% resistance=15k package=THT]
  R6 = Resistor [tolerance=±5% resistance=10k package=THT]
  TRS3 = Audio Jack (TRS) 3.5mm [package="4Ucon 08780 [THT]"]
  R7 = Resistor [tolerance=±5% resistance=15k package=THT]
  R8 = Resistor [tolerance=±5% resistance=10k package=THT]
  TRS4 = Audio Jack (TRS) 3.5mm [package="4Ucon 08780 [THT]"]
  R9 = Resistor [tolerance=±5% resistance=15k package=THT]
  R10 = Resistor [tolerance=±5% resistance=10k package=THT]
  TRS5 = Audio Jack (TRS) 3.5mm [package="4Ucon 08780 [THT]"]
  LED1 = RGB LED (com. cathode, rbg) [package="5 mm [THT]"]
  S1 = Momentary Switch [package=ksa_sealed_tac_switch]
  R11 = Resistor [tolerance=±5% resistance=10k package=THT]
  R12 = Resistor [tolerance=±5% resistance=2.2k package=THT]
  R13 = Resistor [tolerance=±5% resistance=1k package=THT]
  S2 = Toggle Switch [package=THT]

nets:
  N1: Bauteil1.D8, R1.Pin_1, R2.Pin_1
  N2: Bauteil1.D9_PWM, R3.Pin_1, R4.Pin_1
  N3: Bauteil1.D10_PWM/SS, R5.Pin_1, R6.Pin_1
  N4: Bauteil1.D11_PWM/MOSI, R7.Pin_1, R8.Pin_1
  N5: Bauteil1.D12/MISO, R9.Pin_1, R10.Pin_1
  N6: Bauteil1.D13/SCK, S1.3, R11.Pin_1
  N7: Bauteil1.D2, R13.Pin_0
  N8: Bauteil1.D3_PWM, JY-MCU.TX
  N9: Bauteil1.D6_PWM, LED1.green_anode
  N10: Bauteil1.D7, LED1.red_anode
  5V: Bauteil1.5V, JY-MCU.VCC, S1.1
  GND: Bauteil1.GND, JY-MCU.GND, R2.Pin_0, Power_plug1.GND, TRS1.Sleeve, R4.Pin_0, TRS2.Sleeve, R6.Pin_0, TRS3.Sleeve, TRS4.Sleeve, R10.Pin_0, TRS5.Sleeve, LED1.common_cathode, R11.Pin_0, R12.Pin_0
  N11: JY-MCU.RX, R12.Pin_1, R13.Pin_1
  N12: R1.Pin_0, TRS1.Tip
  N13: Power_plug1.VCC, S2.L1
  N14: TRS1.Ring, TRS2.Ring, TRS3.Ring, TRS4.Ring, TRS5.Ring, S2.COM
  N15: R3.Pin_0, TRS2.Tip
  N16: R5.Pin_0, TRS3.Tip
  N17: R7.Pin_0, TRS4.Tip
  N18: R9.Pin_0, TRS5.Tip

notes:
  Reset
  Photoelectric Sensors:
  E30-R4NA 6-36VDC NPN NO 3

custom parts:
  JY-MCU: Description: The Bluetooth Mate is very similar to our BlueSMiRF modem, but it is designed specifically to be used with our Arduino Pros and LilyPad Arduinos. These modems work as a serial (RX/TX) pipe, and are a great wireless replacement for serial cables. Any serial stream from 9600 to 115200bps can be passed seamlessly from your computer to your target. Bluetooth Mate has the same pin out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

// code stored in the sketch: stoppuhr.ino

